// Logisim project schemes.circ as structural Verilog: 2 circuits, main circuit DataPath
module DataPath (
  input  in_1,
  input  in_2,
  input  in_3,
  input  in_4,
  input  in_5,
  input  in_6,
  input  in_7,
  input  in_8,
  input  in_9,
  input  in_10,
  input  in_11,
  input  in_12,
  input  in_13,
  input  in_14,
  input  [2:0] in_15,
  input  [3:0] in_16,
  input  in_17,
  output [31:0] out_18,
  output [31:0] out_19,
  output [2:0] out_20
);

  wire and_1_out, and_2_out, and_4_out, demultiplexer_1_out0, demultiplexer_1_out1, demultiplexer_1_out2,
       demultiplexer_1_out3, demultiplexer_1_out4, demultiplexer_1_out5, demultiplexer_1_out6,
       demultiplexer_1_out7, demultiplexer_1_out8, demultiplexer_1_out9, demultiplexer_1_out10,
       demultiplexer_1_out11, demultiplexer_1_out12, demultiplexer_1_out13, demultiplexer_1_out14,
       demultiplexer_1_out15, demultiplexer_2_out0, demultiplexer_2_out1, demultiplexer_3_out0,
       demultiplexer_3_out1, demultiplexer_3_out2, demultiplexer_3_out3, or_1_out;
  wire [2:0] comparator_1_lt;
  wire [31:0] adder_1_out, and_3_out, controlled_buffer_1_out, controlled_buffer_2_out, divider_1_out,
       multiplexer_1_out, multiplexer_2_out, multiplexer_3_out, multiplier_1_out, not_1_out, register_1_q,
       register_2_q, register_3_q, register_4_q, register_5_q, register_6_q, register_7_q, register_8_q,
       register_10_q, register_11_q, register_13_q, register_14_q, register_15_q, register_16_q,
       register_18_q, register_19_q, register_20_q, register_21_q, register_22_q, register_23_q,
       register_24_q, register_25_q, shifter_1_out, shifter_2_out;

  Register #(.width(32)) register_1 (
    .D(controlled_buffer_2_out), .Q(register_1_q), .clk(demultiplexer_1_out0));  // open: en, clr
  Register #(.width(32)) register_2 (
    .D(controlled_buffer_2_out), .Q(register_2_q), .clk(demultiplexer_1_out1));  // open: en, clr
  Register #(.width(32)) register_3 (
    .D(controlled_buffer_2_out), .Q(register_3_q), .clk(demultiplexer_1_out2));  // open: en, clr
  Register #(.width(32)) register_4 (
    .D(controlled_buffer_2_out), .Q(register_4_q), .clk(demultiplexer_1_out3));  // open: en, clr
  Register #(.width(32)) register_5 (
    .D(controlled_buffer_2_out), .Q(register_5_q), .clk(demultiplexer_1_out4));  // open: en, clr
  Register #(.width(32)) register_6 (
    .D(controlled_buffer_2_out), .Q(register_6_q), .clk(demultiplexer_1_out5));  // open: en, clr
  Register #(.width(32)) register_7 (
    .D(controlled_buffer_2_out), .Q(register_7_q), .clk(demultiplexer_1_out6));  // open: en, clr
  Register #(.width(32)) register_8 (
    .D(controlled_buffer_2_out), .Q(register_8_q), .clk(demultiplexer_1_out7));  // open: en, clr
  Demultiplexer #(.select(4)) demultiplexer_1 (
    .out0(demultiplexer_1_out0), .out1(demultiplexer_1_out1), .out2(demultiplexer_1_out2),
    .out3(demultiplexer_1_out3), .out4(demultiplexer_1_out4), .out5(demultiplexer_1_out5),
    .out6(demultiplexer_1_out6), .out7(demultiplexer_1_out7), .out8(demultiplexer_1_out8),
    .out9(demultiplexer_1_out9), .out10(demultiplexer_1_out10), .out11(demultiplexer_1_out11),
    .out12(demultiplexer_1_out12), .out13(demultiplexer_1_out13), .out14(demultiplexer_1_out14),
    .out15(demultiplexer_1_out15), .in(in_14), .sel(in_16));  // open: en
  Register #(.width(32)) register_9 (
    .D(controlled_buffer_2_out), .Q(out_19), .clk(demultiplexer_1_out15));  // open: en, clr
  Register #(.width(32)) register_10 (
    .D(controlled_buffer_2_out), .Q(register_10_q), .clk(demultiplexer_1_out14));  // open: en, clr
  Register #(.width(32)) register_11 (
    .D(controlled_buffer_2_out), .Q(register_11_q), .clk(demultiplexer_1_out13));  // open: en, clr
  Register #(.width(32)) register_12 (
    .D(controlled_buffer_2_out), .Q(out_18), .clk(demultiplexer_1_out12));  // open: en, clr
  Register #(.width(32)) register_13 (
    .D(controlled_buffer_2_out), .Q(register_13_q), .clk(demultiplexer_1_out11));  // open: en, clr
  Register #(.width(32)) register_14 (
    .D(controlled_buffer_2_out), .Q(register_14_q), .clk(demultiplexer_1_out10));  // open: en, clr
  Register #(.width(32)) register_15 (
    .D(controlled_buffer_2_out), .Q(register_15_q), .clk(demultiplexer_1_out9));  // open: en, clr
  Register #(.width(32)) register_16 (
    .D(controlled_buffer_2_out), .Q(register_16_q), .clk(demultiplexer_1_out8));  // open: en, clr
  Multiplexer #(.select(4), .width(32)) multiplexer_1 (
    .in0(register_1_q), .in1(register_2_q), .in2(register_3_q), .in3(register_4_q), .in4(out_19),
    .in5(register_10_q), .in6(register_11_q), .in7(out_18), .in8(register_13_q), .in9(register_14_q),
    .in10(register_15_q), .in11(register_16_q), .in12(register_5_q), .in13(register_6_q),
    .in14(register_7_q), .in15(register_8_q), .out(multiplexer_1_out), .sel(in_16));  // open: en
  Register #(.width(3)) register_17 (.D(comparator_1_lt), .Q(out_20), .clk(in_17));  // open: en, clr
  Register #(.width(32)) register_18 (.D(controlled_buffer_2_out), .Q(register_18_q), .clk(in_1));  // open: en, clr
  Register #(.width(32)) register_19 (
    .D(controlled_buffer_2_out), .Q(register_19_q), .clk(in_6), .clr(in_7));  // open: en
  and and_1 (and_1_out, in_12, out_20[2]);
  Register #(.width(32)) register_20 (.D(multiplexer_1_out), .Q(register_20_q), .clk(in_8), .clr(in_9));  // open: en
  or or_1 (or_1_out, in_10, and_1_out);
  and and_2 (and_2_out, register_18_q[12], register_18_q[2], register_18_q[3], register_18_q[4], register_18_q[5], register_18_q[6], register_18_q[7], register_18_q[8], register_18_q[9], register_18_q[10], register_18_q[11], register_18_q[13], register_18_q[14], register_18_q[15], register_18_q[16], register_18_q[17], register_18_q[18], register_18_q[19], register_18_q[20], register_18_q[21], register_18_q[22], register_18_q[23]);
  Demultiplexer demultiplexer_2 (
    .out0(demultiplexer_2_out0), .out1(demultiplexer_2_out1), .in(in_2), .sel(and_2_out));  // open: en
  assign controlled_buffer_1_out = in_5 ? register_19_q : 32'bz;  // Controlled_Buffer controlled_buffer_1
  assign controlled_buffer_2_out = in_4 ? controlled_buffer_1_out : 32'bz;  // Controlled_Buffer controlled_buffer_2
  assign controlled_buffer_1_out = in_4 ? multiplexer_3_out : 32'bz;  // Controlled_Buffer controlled_buffer_3
  assign and_3_out = register_20_q & register_19_q;  // AND_Gate and_3, 32 bits wide
  assign not_1_out = ~register_19_q;  // NOT_Gate not_1, 32 bits wide
  Adder #(.width(32)) adder_1 (
    .a(register_20_q), .b(register_19_q), .out(adder_1_out), .cin(or_1_out), .cout(comparator_1_lt[2]));
  Shifter #(.width(32)) shifter_1 (.in(register_20_q), .\dist (register_19_q[4:0]), .out(shifter_1_out));
  Shifter #(.width(32), .shift("lr")) shifter_2 (.in(register_20_q), .\dist (register_19_q[4:0]), .out(shifter_2_out));
  Multiplier #(.width(32)) multiplier_1 (
    .a(register_20_q), .b(register_19_q), .out(multiplier_1_out));  // open: cin, cout
  Divider #(.width(32)) divider_1 (.a(register_20_q), .b(register_19_q), .out(divider_1_out));  // open: upper, rem
  RAM #(.addrWidth(24), .dataWidth(32)) ram_1 (
    .addr(register_18_q[23:0]), .data(controlled_buffer_1_out), .sel(demultiplexer_2_out0), .clk(in_3),
    .ld(in_4));  // open: clr
  and and_4 (and_4_out, in_3, demultiplexer_2_out1);
  Multiplexer #(.select(3), .width(32)) multiplexer_2 (
    .in0(and_3_out), .in1(not_1_out), .in2(adder_1_out), .in3(shifter_1_out), .in4(shifter_2_out),
    .in5({{16{1'b0}}, register_19_q[15:0]}), .in6(multiplier_1_out), .in7(divider_1_out),
    .out(multiplexer_2_out), .sel(in_15));  // open: en
  Demultiplexer #(.select(2)) demultiplexer_3 (
    .out0(demultiplexer_3_out0), .out1(demultiplexer_3_out1), .out2(demultiplexer_3_out2),
    .out3(demultiplexer_3_out3), .in(and_4_out), .sel(register_18_q[1:0]));  // open: en
  Comparator #(.width(32)) comparator_1 (
    .a(multiplexer_2_out), .b({32{1'b0}}), .eq(comparator_1_lt[1]), .lt(comparator_1_lt[0]));  // open: gt
  Register #(.width(32)) register_21 (.D(multiplexer_2_out), .Q(register_21_q), .clk(in_11));  // open: en, clr
  Register #(.width(32)) register_22 (
    .D(controlled_buffer_1_out), .Q(register_22_q), .clk(demultiplexer_3_out0));  // open: en, clr
  Register #(.width(32)) register_23 (
    .D(controlled_buffer_1_out), .Q(register_23_q), .clk(demultiplexer_3_out1));  // open: en, clr
  Register #(.width(32)) register_24 (
    .D(controlled_buffer_1_out), .Q(register_24_q), .clk(demultiplexer_3_out2));  // open: en, clr
  Register #(.width(32)) register_25 (
    .D(controlled_buffer_1_out), .Q(register_25_q), .clk(demultiplexer_3_out3));  // open: en, clr
  assign controlled_buffer_2_out = in_13 ? register_21_q : 32'bz;  // Controlled_Buffer controlled_buffer_4
  Multiplexer #(.select(2), .width(32)) multiplexer_3 (
    .in0(register_22_q), .in1(register_23_q), .in2(register_24_q), .in3(register_25_q),
    .out(multiplexer_3_out), .sel(register_18_q[1:0]));  // open: en

  // Notes on the sheet:
  //   R0
  //   R1
  //   R2
  //   R3
  //   R4
  //   R5
  //   R6
  //   R7
  //   IR
  //   PC
  //   SP
  //   INTR
  //   R8
  //   R9
  //   R10
  //   R11
endmodule

module ControlUnit (
  input  in_1,
  input  [31:0] in_2,
  input  [2:0] flags,
  output [3:0] Reg,
  output setReg,
  output setAR,
  output setDR,
  output resetDR,
  output readFromMem,
  output writeToMem,
  output DROnBus,
  output selectMem,
  output setFirstALU,
  output resetFirstALU,
  output setOutALU,
  output setFlags,
  output useCarry,
  output PLUS1,
  output ALU2Regs,
  output [2:0] out_20
);

  wire and_1_out, and_2_out, comparator_1_eq, comparator_2_eq, comparator_3_eq, not_1_out, or_1_out,
       or_2_out, or_3_out, or_4_out, or_5_out;
  wire [5:0] demultiplexer_1_out0_3, multiplexer_1_out;
  wire [7:0] counter_1_q, demultiplexer_1_out0_2, multiplexer_2_out;
  wire [21:0] demultiplexer_1_out0;
  wire [22:0] rom_1_data;

  not not_1 (not_1_out, or_1_out);
  Counter counter_1 (
    .load(not_1_out), .D(multiplexer_2_out), .count(or_1_out), .Q(counter_1_q), .clk(in_1));  // open: carry, clr
  Multiplexer #(.width(6)) multiplexer_1 (
    .in0(in_2[26:21]), .in1(demultiplexer_1_out0_3), .out(multiplexer_1_out), .sel(demultiplexer_1_out0[11]));  // open: en
  Comparator #(.width(1)) comparator_1 (.a(flags[0]), .b(multiplexer_1_out[4]), .eq(comparator_1_eq));  // open: gt, lt
  Comparator #(.width(1)) comparator_2 (.a(multiplexer_1_out[2]), .b(flags[1]), .eq(comparator_2_eq));  // open: gt, lt
  Comparator #(.width(1)) comparator_3 (.a(multiplexer_1_out[0]), .b(flags[2]), .eq(comparator_3_eq));  // open: gt, lt
  or or_1 (or_1_out, rom_1_data[22], ~and_1_out);  // OR_Gate
  Multiplexer #(.width(8)) multiplexer_2 (
    .in0({3'b000, in_2[31:27]}), .in1(demultiplexer_1_out0_2), .out(multiplexer_2_out),
    .sel(demultiplexer_1_out0[1]));  // open: en
  or or_2 (or_2_out, ~multiplexer_1_out[5], comparator_1_eq);  // OR_Gate
  or or_3 (or_3_out, ~multiplexer_1_out[3], comparator_2_eq);  // OR_Gate
  or or_4 (or_4_out, ~multiplexer_1_out[1], comparator_3_eq);  // OR_Gate
  and and_1 (and_1_out, demultiplexer_1_out0[0], or_5_out);
  or or_5 (or_5_out, ~demultiplexer_1_out0[10], and_2_out);  // OR_Gate
  and and_2 (and_2_out, or_2_out, or_3_out, or_4_out);
  ROM #(.dataWidth(23)) rom_1 (.addr(counter_1_q), .data(rom_1_data));  // open: sel
  Demultiplexer #(.width(22)) demultiplexer_1 (
    .out0({demultiplexer_1_out0[21:18], demultiplexer_1_out0_3, demultiplexer_1_out0[11:10], demultiplexer_1_out0_2, demultiplexer_1_out0[1:0]}),
    .out1({out_20, ALU2Regs, PLUS1, useCarry, setFlags, setOutALU, resetFirstALU, setFirstALU, selectMem, DROnBus, writeToMem, readFromMem, resetDR, setDR, setAR, setReg, Reg}),
    .in(rom_1_data[21:0]), .sel(rom_1_data[22]));  // open: en

  // Notes on the sheet:
  //   IR
  //   N
  //   Z
  //   C
  //   contents of rom_1 (hex, n*v repeats v):
  //   30c01
  //   ALUOperation
endmodule
